// Digital circuit 36bExpand.dig as structural Verilog
module _36bExpand (
  input  In,
  output [35:0] Out
);

  _32bExpand _32bexpand_1 (.In(In), .Out(Out[31:0]));

  assign Out[35:32] = {4{In}};
endmodule
