// Digital circuit ALU.dig as structural Verilog
module ALU (
  input  [31:0] A,
  input  [31:0] B,
  input  F_0,
  input  F_1,
  input  ENA,
  input  ENB,
  input  INVA,
  input  INC,
  output [31:0] C,
  output CF,
  output OF,
  output NF,
  output ZF
);

  wire and_3_out, and_4_out, and_5_out, and_6_out, not_1_out, not_3_out, not_4_out, not_5_out;
  wire [30:0] _32badder_1_p4;
  wire [31:0] _32bexpand_1_out, _32bexpand_2_out, _32bexpand_3_out, _32bexpand_4_out, _32bexpand_5_out,
       _32bexpand_6_out, _32bexpand_7_out, and_1_out, and_2_out, and_7_out, and_8_out, and_9_out, and_10_out,
       and_11_out, not_6_out, or_1_out, xor_1_out;

  _32bExpand _32bexpand_1 (.In(INVA), .Out(_32bexpand_1_out));
  _32bExpand _32bexpand_2 (.In(ENA), .Out(_32bexpand_2_out));
  _32bExpand _32bexpand_3 (.In(ENB), .Out(_32bexpand_3_out));
  assign and_1_out = A & _32bexpand_2_out;  // And and_1, 32 bits wide
  assign and_2_out = B & _32bexpand_3_out;  // And and_2, 32 bits wide
  not not_1 (not_1_out, F_0);
  not not_2 (not_1_out, F_0);
  not not_3 (not_3_out, F_1);
  not not_4 (not_4_out, F_0);
  not not_5 (not_5_out, F_1);
  assign xor_1_out = _32bexpand_1_out ^ and_1_out;  // XOr xor_1, 32 bits wide
  and and_3 (and_3_out, not_1_out, not_3_out);
  and and_4 (and_4_out, not_4_out, F_1);
  and and_5 (and_5_out, F_0, not_5_out);
  and and_6 (and_6_out, F_0, F_1);
  _32bExpand _32bexpand_4 (.In(and_3_out), .Out(_32bexpand_4_out));
  _32bExpand _32bexpand_5 (.In(and_4_out), .Out(_32bexpand_5_out));
  _32bExpand _32bexpand_6 (.In(and_5_out), .Out(_32bexpand_6_out));
  _32bExpand _32bexpand_7 (.In(and_6_out), .Out(_32bexpand_7_out));
  assign and_7_out = xor_1_out & and_2_out;  // And and_7, 32 bits wide
  assign or_1_out = xor_1_out | and_2_out;  // Or or_1, 32 bits wide
  assign not_6_out = ~and_2_out;  // Not not_6, 32 bits wide
  assign and_8_out = and_7_out & _32bexpand_4_out;  // And and_8, 32 bits wide
  assign and_9_out = or_1_out & _32bexpand_5_out;  // And and_9, 32 bits wide
  assign and_10_out = not_6_out & _32bexpand_6_out;  // And and_10, 32 bits wide
  // _32bAdder _32badder_1: pin names not known; wires that end beside it: INC, xor_1_out, and_2_out, {NF, _32badder_1_p4}, CF, OF
  assign and_11_out = _32bexpand_7_out & {NF, _32badder_1_p4};  // And and_11, 32 bits wide
  Comparator #(.Bits(32)) comparator_1 (.a({NF, _32badder_1_p4}), .b({32{1'b0}}), .eq(ZF));  // open: gt, lt
  assign C = and_8_out | and_9_out | and_10_out | and_11_out;  // Or or_2, 32 bits wide
endmodule
