// Digital circuit 16bAdder.dig as structural Verilog
module _16bAdder (
  input  [15:0] A,
  input  [15:0] B,
  input  c_I,
  output [15:0] O,
  output CF,
  output OF
);

  wire _8badder_1_cf;

  _8bAdder _8badder_1 (.c_I(c_I), .A(A[7:0]), .B(B[7:0]), .O(O[7:0]), .CF(_8badder_1_cf));  // open: OF
  _8bAdder _8badder_2 (.c_I(_8badder_1_cf), .A(A[15:8]), .B(B[15:8]), .O(O[15:8]), .CF(CF), .OF(OF));
endmodule
