// Digital circuit 32bAdder.dig as structural Verilog
module _32bAdder (
  input  c_I,
  input  [31:0] A,
  input  [31:0] B,
  output [31:0] O,
  output CF,
  output OF
);

  wire _16badder_1_cf;

  _16bAdder _16badder_1 (.A(A[15:0]), .B(B[15:0]), .c_I(c_I), .O(O[15:0]), .CF(_16badder_1_cf));  // open: OF
  _16bAdder _16badder_2 (.A(A[31:16]), .B(B[31:16]), .c_I(_16badder_1_cf), .O(O[31:16]), .CF(CF), .OF(OF));
  // Pins of 1 and 32 bits meet at O
endmodule
