// Digital circuit 4bAdder.dig as structural Verilog
module _4bAdder (
  input  [3:0] A,
  input  [3:0] B,
  input  c_I,
  output CF,
  output [3:0] O,
  output OF
);

  wire fa_1_c, fa_2_c, fa_3_c;

  FA fa_1 (.A(A[0]), .B(B[0]), .C_IN(c_I), .O(O[0]), .C(fa_1_c));
  FA fa_2 (.A(A[1]), .B(B[1]), .C_IN(fa_1_c), .O(O[1]), .C(fa_2_c));
  FA fa_3 (.A(A[2]), .B(B[2]), .C_IN(fa_2_c), .O(O[2]), .C(fa_3_c));
  FA fa_4 (.A(A[3]), .B(B[3]), .C_IN(fa_3_c), .O(O[3]), .C(CF));
  xor xor_1 (OF, fa_3_c, CF);
endmodule
