// Digital circuit 8bAdder.dig as structural Verilog
module _8bAdder (
  input  c_I,
  input  [7:0] A,
  input  [7:0] B,
  output [7:0] O,
  output CF,
  output OF
);

  wire _4badder_1_cf;

  _4bAdder _4badder_1 (.A(A[3:0]), .B(B[3:0]), .c_I(c_I), .CF(_4badder_1_cf), .O(O[3:0]));  // open: OF
  _4bAdder _4badder_2 (.A(A[7:4]), .B(B[7:4]), .c_I(_4badder_1_cf), .CF(CF), .O(O[7:4]), .OF(OF));
endmodule
