// Digital circuit FA.dig as structural Verilog
module FA (
  input  A,
  input  B,
  input  C_IN,
  output O,
  output C
);

  wire and_1_out, and_2_out, xor_1_out;

  xor xor_1 (xor_1_out, A, B);
  and and_1 (and_1_out, A, B);
  and and_2 (and_2_out, C_IN, xor_1_out);
  xor xor_2 (O, C_IN, xor_1_out);
  or or_1 (C, and_2_out, and_1_out);
endmodule
