// Digital circuit ChangeDetector.dig as structural Verilog
module ChangeDetector (
  input  [31:0] I,
  output O
);

  wire [5:0] bitcount_1_out;
  wire [31:0] and_1_out, delay_1_out, delay_2_out, delay_3_out, not_1_out, not_2_out, not_3_out;

  assign not_1_out = ~I;  // Not not_1, 32 bits wide
  Delay #(.Bits(32)) delay_1 (.in(I), .out(delay_1_out));
  assign not_2_out = ~not_1_out;  // Not not_2, 32 bits wide
  assign not_3_out = ~delay_1_out;  // Not not_3, 32 bits wide
  Delay #(.Bits(32), .delayTime(20)) delay_2 (.in(not_2_out), .out(delay_2_out));
  Delay #(.Bits(32), .delayTime(20)) delay_3 (.in(not_3_out), .out(delay_3_out));
  assign and_1_out = not_1_out & delay_2_out;  // And and_1, 32 bits wide
  assign and_1_out = delay_3_out & delay_1_out;  // And and_2, 32 bits wide
  BitCount #(.Bits(32)) bitcount_1 (.in(and_1_out), .out(bitcount_1_out));
  Comparator #(.Bits(6)) comparator_1 (.a({6{1'b0}}), .b(bitcount_1_out), .lt(O));  // open: gt, eq
endmodule
