// Digital circuit 32bAExtended32b(8b).dig as structural Verilog
module _32bAExtended32b_8b (
  input  [31:0] ADDR,
  input  [31:0] D_I,
  input  C,
  output [31:0] D_O
);

  wire and_1_out, not_1_out;

  not not_1 (not_1_out, C);
  and and_1 (and_1_out, C, not_1_out);
  _8bA8b _8ba8b_1 (.ADDR(ADDR[7:0]), .D_I(D_I[7:0]), .C(and_1_out), .D_O(D_O[7:0]));
  _8bA8b _8ba8b_2 (.ADDR(ADDR[7:0]), .D_I(D_I[15:8]), .C(and_1_out), .D_O(D_O[15:8]));
  _8bA8b _8ba8b_3 (.ADDR(ADDR[7:0]), .D_I(D_I[23:16]), .C(and_1_out), .D_O(D_O[23:16]));
  _8bA8b _8ba8b_4 (.ADDR(ADDR[7:0]), .D_I(D_I[31:24]), .C(and_1_out), .D_O(D_O[31:24]));
endmodule
