// Digital circuit 8b2w.dig as structural Verilog
module _8b2w (
  input  ADDR,
  input  [7:0] D_I,
  input  C,
  output [7:0] D_O
);

  wire [7:0] d_ff_1_q, d_ff_2_q, demultiplexer_1_out_0, demultiplexer_1_out_1;

  Demultiplexer #(.Bits(8)) demultiplexer_1 (
    .sel(ADDR), .in(D_I), .out_0(demultiplexer_1_out_0), .out_1(demultiplexer_1_out_1));
  D_FF #(.Bits(8)) d_ff_1 (.D(demultiplexer_1_out_0), .C(C), .Q(d_ff_1_q));  // open: nQ
  D_FF #(.Bits(8)) d_ff_2 (.D(demultiplexer_1_out_1), .C(C), .Q(d_ff_2_q));  // open: nQ
  Multiplexer #(.Bits(8)) multiplexer_1 (.sel(ADDR), .in_0(d_ff_1_q), .in_1(d_ff_2_q), .out(D_O));
  // Pins of 1 and 8 bits meet at D_O
endmodule
