// Digital circuit 8bA1b.dig as structural Verilog
module _8bA1b (
  input  ADDR,
  input  [7:0] D_I,
  input  C,
  output [7:0] D_O
);

  wire and_1_out, and_2_out, not_1_out;
  wire [7:0] d_ff_1_q, d_ff_2_q, demultiplexer_1_out_0, demultiplexer_1_out_1;

  Demultiplexer #(.Bits(8)) demultiplexer_1 (
    .sel(ADDR), .in(D_I), .out_0(demultiplexer_1_out_0), .out_1(demultiplexer_1_out_1));
  not not_1 (not_1_out, ADDR);
  and and_1 (and_1_out, C, not_1_out);
  and and_2 (and_2_out, C, ADDR);
  D_FF #(.Bits(8)) d_ff_1 (.D(demultiplexer_1_out_0), .C(and_1_out), .Q(d_ff_1_q));  // open: nQ
  D_FF #(.Bits(8)) d_ff_2 (.D(demultiplexer_1_out_1), .C(and_2_out), .Q(d_ff_2_q));  // open: nQ
  Multiplexer #(.Bits(8)) multiplexer_1 (.sel(ADDR), .in_0(d_ff_1_q), .in_1(d_ff_2_q), .out(D_O));
endmodule
