// Digital circuit 8bA2b.dig as structural Verilog
module _8bA2b (
  input  [1:0] ADDR,
  input  [7:0] D_I,
  input  C,
  output [7:0] D_O
);

  wire and_1_out, and_2_out, and_3_out, and_4_out, not_1_out, not_2_out;
  wire [7:0] _8ba1b_1_d_o, _8ba1b_2_d_o, demultiplexer_1_out_0, demultiplexer_1_out_1;

  Demultiplexer #(.Bits(8)) demultiplexer_1 (
    .sel(ADDR[1]), .in(D_I), .out_0(demultiplexer_1_out_0), .out_1(demultiplexer_1_out_1));
  not not_1 (not_1_out, ADDR[1]);
  not not_2 (not_2_out, ADDR[1]);
  and and_1 (and_1_out, not_1_out, ADDR[0]);
  and and_2 (and_2_out, C, not_2_out);
  and and_3 (and_3_out, ADDR[1], ADDR[0]);
  and and_4 (and_4_out, C, ADDR[1]);
  _8bA1b _8ba1b_1 (.ADDR(and_1_out), .D_I(demultiplexer_1_out_0), .C(and_2_out), .D_O(_8ba1b_1_d_o));
  _8bA1b _8ba1b_2 (.ADDR(and_3_out), .D_I(demultiplexer_1_out_1), .C(and_4_out), .D_O(_8ba1b_2_d_o));
  Multiplexer #(.Bits(8)) multiplexer_1 (.sel(ADDR[1]), .in_0(_8ba1b_1_d_o), .in_1(_8ba1b_2_d_o), .out(D_O));
endmodule
