// Digital circuit 8bA5b.dig as structural Verilog
module _8bA5b (
  input  [4:0] ADDR,
  input  [7:0] D_I,
  input  C,
  output [7:0] D_O
);

  wire and_2_out, and_4_out, not_1_out, not_2_out;
  wire [3:0] _4bexpand_1_o, _4bexpand_2_o, and_1_out, and_3_out;
  wire [7:0] _8ba4b_1_d_o, _8ba4b_2_d_o, demultiplexer_1_out_0, demultiplexer_1_out_1;

  Demultiplexer #(.Bits(8)) demultiplexer_1 (
    .sel(ADDR[4]), .in(D_I), .out_0(demultiplexer_1_out_0), .out_1(demultiplexer_1_out_1));
  not not_1 (not_1_out, ADDR[4]);
  not not_2 (not_2_out, ADDR[4]);
  _4bExpand _4bexpand_1 (.I(not_1_out), .O(_4bexpand_1_o));
  _4bExpand _4bexpand_2 (.I(ADDR[4]), .O(_4bexpand_2_o));
  assign and_1_out = _4bexpand_1_o & ADDR[3:0];  // And and_1, 4 bits wide
  and and_2 (and_2_out, C, not_2_out);
  assign and_3_out = _4bexpand_2_o & ADDR[3:0];  // And and_3, 4 bits wide
  and and_4 (and_4_out, C, ADDR[4]);
  _8bA4b _8ba4b_1 (.ADDR(and_1_out), .D_I(demultiplexer_1_out_0), .C(and_2_out), .D_O(_8ba4b_1_d_o));
  _8bA4b _8ba4b_2 (.ADDR(and_3_out), .D_I(demultiplexer_1_out_1), .C(and_4_out), .D_O(_8ba4b_2_d_o));
  Multiplexer #(.Bits(8)) multiplexer_1 (.sel(ADDR[4]), .in_0(_8ba4b_1_d_o), .in_1(_8ba4b_2_d_o), .out(D_O));
endmodule
