// Digital circuit 8bA8b.dig as structural Verilog
module _8bA8b (
  input  [7:0] ADDR,
  input  [7:0] D_I,
  input  C,
  output [7:0] D_O
);

  wire and_2_out, and_4_out, not_1_out, not_2_out;
  wire [6:0] _7bexpand_1_o, _7bexpand_2_o, and_1_out, and_3_out;
  wire [7:0] _8ba7b_1_d_o, _8ba7b_2_d_o, demultiplexer_1_out_0, demultiplexer_1_out_1;

  Demultiplexer #(.Bits(8)) demultiplexer_1 (
    .sel(ADDR[7]), .in(D_I), .out_0(demultiplexer_1_out_0), .out_1(demultiplexer_1_out_1));
  not not_1 (not_1_out, ADDR[7]);
  not not_2 (not_2_out, ADDR[7]);
  _7bExpand _7bexpand_1 (.I(not_1_out), .O(_7bexpand_1_o));
  _7bExpand _7bexpand_2 (.I(ADDR[7]), .O(_7bexpand_2_o));
  assign and_1_out = _7bexpand_1_o & ADDR[6:0];  // And and_1, 7 bits wide
  and and_2 (and_2_out, C, not_2_out);
  assign and_3_out = _7bexpand_2_o & ADDR[6:0];  // And and_3, 7 bits wide
  and and_4 (and_4_out, C, ADDR[7]);
  _8bA7b _8ba7b_1 (.ADDR(and_1_out), .D_I(demultiplexer_1_out_0), .C(and_2_out), .D_O(_8ba7b_1_d_o));
  _8bA7b _8ba7b_2 (.ADDR(and_3_out), .D_I(demultiplexer_1_out_1), .C(and_4_out), .D_O(_8ba7b_2_d_o));
  Multiplexer #(.Bits(8)) multiplexer_1 (.sel(ADDR[7]), .in_0(_8ba7b_1_d_o), .in_1(_8ba7b_2_d_o), .out(D_O));
endmodule
