// Digital circuit RisingFallingD.dig as structural Verilog
module RisingFallingD (
  input  [31:0] D_rising,
  input  En_rising,
  input  [31:0] D_falling,
  input  En_falling,
  input  C,
  output [31:0] Q
);

  wire and_3_out, and_4_out, and_5_out, and_6_out, delay_1_out, not_1_out, not_2_out, not_3_out, not_4_out,
       or_2_out;
  wire [31:0] _32bexpand_1_out, _32bexpand_2_out, and_1_out, and_2_out, or_1_out;

  not not_1 (not_1_out, C);
  _32bExpand _32bexpand_1 (.In(not_1_out), .Out(_32bexpand_1_out));
  _32bExpand _32bexpand_2 (.In(C), .Out(_32bexpand_2_out));
  not not_2 (not_2_out, C);
  Delay delay_1 (.in(C), .out(delay_1_out));
  assign and_1_out = D_falling & _32bexpand_1_out;  // And and_1, 32 bits wide
  assign and_2_out = D_rising & _32bexpand_2_out;  // And and_2, 32 bits wide
  not not_3 (not_3_out, not_2_out);
  not not_4 (not_4_out, delay_1_out);
  and and_3 (and_3_out, not_2_out, not_3_out);
  and and_4 (and_4_out, not_4_out, delay_1_out);
  assign or_1_out = and_1_out | and_2_out;  // Or or_1, 32 bits wide
  and and_5 (and_5_out, and_3_out, En_falling);
  and and_6 (and_6_out, and_4_out, En_rising);
  or or_2 (or_2_out, and_5_out, and_6_out);
  D_FF #(.Bits(32)) d_ff_1 (.D(or_1_out), .C(or_2_out), .Q(Q));  // open: nQ
endmodule
