// Digital circuit StorageInit8b.dig as structural Verilog
module StorageInit8b (
  input  GO,
  input  CLK_I,
  output [7:0] ADDR,
  output CLK_O,
  output PROG
);

  wire _8badder_1_cf, and_1_out, and_2_out, d_ff_1_nq, edgetrigger_1_o, edgetrigger_2_o, nor_1_out,
       not_1_out, not_2_out, not_3_out, or_1_out;
  wire [7:0] _8badder_1_o, _8bexpand_1_o, and_3_out, d_ff_2_q, d_ff_3_q;

  EdgeTrigger edgetrigger_1 (.C(GO), .O(edgetrigger_1_o));
  RS_FF_AS rs_ff_as_1 (.S(edgetrigger_1_o), .R(edgetrigger_2_o), .Q(PROG));  // open: nQ
  EdgeTrigger edgetrigger_2 (.C(not_1_out), .O(edgetrigger_2_o));
  not not_1 (not_1_out, d_ff_1_nq);
  not not_2 (not_2_out, PROG);
  nor nor_1 (nor_1_out, not_2_out, PROG);
  or or_1 (or_1_out, and_2_out, nor_1_out);
  D_FF d_ff_1 (.D(_8badder_1_cf), .C(or_1_out), .nQ(d_ff_1_nq));  // open: Q
  and and_1 (and_1_out, d_ff_1_nq, PROG);
  and and_2 (and_2_out, CLK_I, and_1_out);
  not not_3 (not_3_out, and_2_out);
  D_FF #(.Bits(8)) d_ff_2 (.D(d_ff_3_q), .C(not_3_out), .Q(d_ff_2_q));  // open: nQ
  _8bAdder _8badder_1 (.c_I(1'b0), .A(d_ff_2_q), .B(8'h1), .O(_8badder_1_o), .CF(_8badder_1_cf));  // open: OF
  _8bExpand _8bexpand_1 (.I(and_1_out), .O(_8bexpand_1_o));
  assign and_3_out = _8badder_1_o & _8bexpand_1_o;  // And and_3, 8 bits wide
  D_FF #(.Bits(8)) d_ff_3 (.D(and_3_out), .C(and_2_out), .Q(d_ff_3_q));  // open: nQ
  assign ADDR = _8bexpand_1_o & d_ff_3_q;  // And and_4, 8 bits wide
  and and_5 (CLK_O, and_2_out, and_1_out);
  // also tied to GND on the sheet: edgetrigger_2_o

  // Notes on the sheet:
  //   CLK_I: Hz: 60
endmodule
