// Digital circuit test.dig as structural Verilog
module test (
  input  [7:0] in_2,
  input  in_3,
  input  clk,
  output [7:0] out_1
);

  wire and_1_out, and_2_out, and_5_out, comparator_1_lt, not_1_out;
  wire [7:0] _8badder_1_o, _8bexpand_1_o, and_3_out, and_4_out, d_ff_1_q, d_ff_2_q, multiplexer_1_out,
       or_1_out;

  Multiplexer #(.Selector_Bits(8), .Bits(8)) multiplexer_1 (
    .sel(or_1_out), .in_0(8'h69), .in_1(8'h1), .in_2(8'h1), .in_3(8'h1), .in_4(8'h1), .in_5(8'h1),
    .in_6(8'h1), .in_7(8'h1), .in_8(8'h1), .in_9(8'h42), .in_10(8'h1), .in_11(8'h1), .in_12(8'h1),
    .in_13(8'h1), .in_14(8'h1), .in_15(8'h1), .in_16(8'h1), .in_17(8'h1), .in_18(8'h1), .in_19(8'h1),
    .in_20(8'h1), .in_21(8'h1), .in_22(8'h1), .in_23(8'h1), .in_24(8'h1), .in_25(8'h1), .in_26(8'h1),
    .in_27(8'h1), .in_28(8'h1), .in_29(8'h1), .in_30(8'h1), .in_31(8'h1), .in_32(8'h1), .in_33(8'h1),
    .in_34(8'h1), .in_35(8'h1), .in_36(8'h1), .in_37(8'h1), .in_38(8'h1), .in_39(8'h1), .in_40(8'h1),
    .in_41(8'h1), .in_42(8'h1), .in_43(8'h1), .in_44(8'h1), .in_45(8'h1), .in_46(8'h1), .in_47(8'h1),
    .in_48(8'h1), .in_49(8'h1), .in_50(8'h1), .in_51(8'h1), .in_52(8'h1), .in_53(8'h1), .in_54(8'h1),
    .in_55(8'h1), .in_56(8'h1), .in_57(8'h1), .in_58(8'h1), .in_59(8'h1), .in_60(8'h1), .in_61(8'h1),
    .in_62(8'h1), .in_63(8'h1), .in_64(8'h1), .in_65(8'h1), .in_66(8'h1), .in_67(8'h1), .in_68(8'h1),
    .in_69(8'h1), .in_70(8'h1), .in_71(8'h1), .in_72(8'h1), .in_73(8'h1), .in_74(8'h1), .in_75(8'h1),
    .in_76(8'h1), .in_77(8'h1), .in_78(8'h1), .in_79(8'h1), .in_80(8'h1), .in_81(8'h1), .in_82(8'h1),
    .in_83(8'h1), .in_84(8'h1), .in_85(8'h1), .in_86(8'h1), .in_87(8'h1), .in_88(8'h1), .in_89(8'h1),
    .in_90(8'h1), .in_91(8'h1), .in_92(8'h1), .in_93(8'h1), .in_94(8'h1), .in_95(8'h1), .in_96(8'h1),
    .in_97(8'h1), .in_98(8'h1), .in_99(8'h1), .in_100(8'h1), .in_101(8'h1), .in_102(8'h1), .in_103(8'h1),
    .in_104(8'h1), .in_105(8'h1), .in_106(8'h1), .in_107(8'h1), .in_108(8'h1), .in_109(8'h1), .in_110(8'h1),
    .in_111(8'h1), .in_112(8'h1), .in_113(8'h1), .in_114(8'h1), .in_115(8'h1), .in_116(8'h1), .in_117(8'h1),
    .in_118(8'h1), .in_119(8'h1), .in_120(8'h1), .in_121(8'h1), .in_122(8'h1), .in_123(8'h1), .in_124(8'h1),
    .in_125(8'h1), .in_126(8'h1), .in_127(8'h1), .in_128(8'h1), .in_129(8'h1), .in_130(8'h1), .in_131(8'h1),
    .in_132(8'h1), .in_133(8'h1), .in_134(8'h1), .in_135(8'h1), .in_136(8'h1), .in_137(8'h1), .in_138(8'h1),
    .in_139(8'h1), .in_140(8'h1), .in_141(8'h1), .in_142(8'h1), .in_143(8'h1), .in_144(8'h1), .in_145(8'h1),
    .in_146(8'h1), .in_147(8'h1), .in_148(8'h1), .in_149(8'h1), .in_150(8'h1), .in_151(8'h1), .in_152(8'h1),
    .in_153(8'h1), .in_154(8'h1), .in_155(8'h1), .in_156(8'h1), .in_157(8'h1), .in_158(8'h1), .in_159(8'h1),
    .in_160(8'h1), .in_161(8'h1), .in_162(8'h1), .in_163(8'h1), .in_164(8'h1), .in_165(8'h1), .in_166(8'h1),
    .in_167(8'h1), .in_168(8'h1), .in_169(8'h1), .in_170(8'h1), .in_171(8'h1), .in_172(8'h1), .in_173(8'h1),
    .in_174(8'h1), .in_175(8'h1), .in_176(8'h1), .in_177(8'h1), .in_178(8'h1), .in_179(8'h1), .in_180(8'h1),
    .in_181(8'h1), .in_182(8'h1), .in_183(8'h1), .in_184(8'h1), .in_185(8'h1), .in_186(8'h1), .in_187(8'h1),
    .in_188(8'h1), .in_189(8'h1), .in_190(8'h1), .in_191(8'h1), .in_192(8'h1), .in_193(8'h1), .in_194(8'h1),
    .in_195(8'h1), .in_196(8'h1), .in_197(8'h1), .in_198(8'h1), .in_199(8'h1), .in_200(8'h1), .in_201(8'h1),
    .in_202(8'h1), .in_203(8'h1), .in_204(8'h1), .in_205(8'h1), .in_206(8'h1), .in_207(8'h1), .in_208(8'h1),
    .in_209(8'h1), .in_210(8'h1), .in_211(8'h1), .in_212(8'h1), .in_213(8'h1), .in_214(8'h1), .in_215(8'h1),
    .in_216(8'h1), .in_217(8'h1), .in_218(8'h1), .in_219(8'h1), .in_220(8'h1), .in_221(8'h1), .in_222(8'h1),
    .in_223(8'h1), .in_224(8'h1), .in_225(8'h1), .in_226(8'h1), .in_227(8'h1), .in_228(8'h1), .in_229(8'h1),
    .in_230(8'h1), .in_231(8'h1), .in_232(8'h1), .in_233(8'h1), .in_234(8'h1), .in_235(8'h1), .in_236(8'h1),
    .in_237(8'h1), .in_238(8'h1), .in_239(8'h1), .in_240(8'h1), .in_241(8'h1), .in_242(8'h1), .in_243(8'h1),
    .in_244(8'h1), .in_245(8'h1), .in_246(8'h1), .in_247(8'h1), .in_248(8'h1), .in_249(8'h1), .in_250(8'h1),
    .in_251(8'h1), .in_252(8'h1), .in_253(8'h1), .in_254(8'h66), .in_255(8'h1), .out(multiplexer_1_out));
  Comparator #(.Bits(8)) comparator_1 (.a(d_ff_2_q), .b({8{1'b1}}), .lt(comparator_1_lt));  // open: gt, eq
  and and_1 (and_1_out, comparator_1_lt, in_3);
  and and_2 (and_2_out, clk, and_1_out);
  D_FF #(.Bits(8)) d_ff_1 (.D(d_ff_2_q), .C(and_2_out), .Q(d_ff_1_q));  // open: nQ
  not not_1 (not_1_out, and_2_out);
  _8bAdder _8badder_1 (.c_I(1'b0), .A(d_ff_1_q), .B(8'h1), .O(_8badder_1_o));  // open: CF, OF
  _8bExpand _8bexpand_1 (.I(and_1_out), .O(_8bexpand_1_o));
  assign and_3_out = _8badder_1_o & _8bexpand_1_o;  // And and_3, 8 bits wide
  D_FF #(.Bits(8)) d_ff_2 (.D(and_3_out), .C(not_1_out), .Q(d_ff_2_q));  // open: nQ
  assign and_4_out = _8bexpand_1_o & d_ff_2_q;  // And and_4, 8 bits wide
  and and_5 (and_5_out, and_2_out, and_1_out);
  assign or_1_out = and_4_out | in_2;  // Or or_1, 8 bits wide
  _8bA8b _8ba8b_1 (.ADDR(or_1_out), .D_I(multiplexer_1_out), .C(and_5_out), .D_O(out_1));

  // Notes on the sheet:
  //   clk: Hz: 5000
endmodule
